// Logisim project lab3.circ as structural Verilog: 1 circuit, main circuit main
module main (
  input  s0,
  input  s1,
  input  s2,
  input  x,
  output n2,
  output n1,
  output n0,
  output y1,
  output y0
);

  wire A_out, B_out, C_out, D_out, E_out, F_out, G_out, H_out, I_out, J_out, K_out, L_out, not_1_out,
       not_2_out, not_3_out, not_4_out;

  not not_1 (not_1_out, s0);
  not not_2 (not_2_out, s1);
  not not_3 (not_3_out, s2);
  not not_4 (not_4_out, x);
  and A (A_out, s1, not_4_out, not_3_out);
  and B (B_out, s1, s0, not_3_out);
  and C (C_out, s2, not_2_out, not_1_out);
  and D (D_out, not_2_out, s0, x);
  and E (E_out, x, s1, s2);
  and F (F_out, not_1_out, s1, x);
  and G (G_out, not_1_out, not_4_out);
  and H (H_out, not_4_out, s2);
  and I (I_out, not_2_out, not_4_out);
  and J (J_out, not_3_out, not_1_out, s1);
  and K (K_out, s1, s2, not_1_out);
  and L (L_out, not_2_out, s0, s2);
  and M (y0, s0, s2);
  or or_1 (n2, A_out, B_out, C_out);
  or or_2 (n1, A_out, D_out, E_out, F_out);
  or or_3 (n0, G_out, H_out, I_out, J_out);
  or or_4 (y1, K_out, L_out);
endmodule
