// Logisim project lab1.circ as structural Verilog: 1 circuit, main circuit main
module main (
  input  x2,
  input  x1,
  input  x0,
  output r
);

  wire A1_out, A2_out, A3_out, not_1_out, not_2_out, not_3_out;

  not not_1 (not_1_out, x2);
  not not_2 (not_2_out, x0);
  not not_3 (not_3_out, x1);
  and A1 (A1_out, not_1_out, x1);
  and A3 (A3_out, x2, not_3_out);
  and A2 (A2_out, A1_out, not_2_out);
  or O (r, A2_out, A3_out);

  // Notes on the sheet:
  //   notX2
  //   notX0
  //   notX1
  //   w1
  //   w3
  //   w2
endmodule
