// Logisim project lab2.circ as structural Verilog: 1 circuit, main circuit main
module main (
  input  x1,
  input  x0,
  input  [1:0] x3_x2,
  output out_4
);

  wire AND_out, XOR_out;

  and AND (AND_out, x1, x0);
  xor XOR (XOR_out, x1, x0);
  Multiplexer #(.select(2), .enable("false")) multiplexer_1 (
    .in0(AND_out), .in1(x0), .in2(x1), .in3(XOR_out), .out(out_4), .sel(x3_x2));

  // Notes on the sheet:
  //   x0
  //   x1
  //   x1x0'+x1'x0
  //   x1x0
endmodule
